# Fritzing sketch temp-device (saved by Fritzing 1.0.2b)
breadboards: 1

parts:
  Part1 = MCP9808 High Accuracy I2C Temperature Sensor [part_number=1782]
  Mod1 = Raspberry Pi Pico W
  OLED2 = 128x64 Monochrom OLED Display with SPI Control

nets:
  VDD: Part1.VDD, Mod1.pin_36, OLED2.3v3
  GND: Part1.GND, Mod1.pin_3, Mod1.pin_8, Mod1.pin_13, Mod1.pin_18, Mod1.pin_23, Mod1.pin_28, Mod1.pin_33, Mod1.pin_38, OLED2.GND
  N1: Part1.SCL, Mod1.pin_27
  N2: Part1.SDA, Mod1.pin_26
  N3: Mod1.pin_22, OLED2.CS
  N4: Mod1.pin_24, OLED2.Clock
  N5: Mod1.pin_25, OLED2.Data
  N6: Mod1.pin_29, OLED2.SA0/DC
  N7: Mod1.pin_30, OLED2.Reset

custom parts:
  MCP9808 High Accuracy I2C Temperature Sensor: This I2C digital temperature sensor is one of the more accurate/precise we've ever seen, with a typical accuracy of ±0.25°C over the sensor's -40°C to +125°C range and precision of +0.0625°C. They work great with any microcontroller using standard i2c. There are 3 address pins so you can connect up to 8 to a single I2C bus without address collisions. Best of all, a wide voltage range makes is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
  Raspberry Pi Pico W: Raspberry Pi Pico W. Based around the RP2040 microcontroller the Pico W is a low cost microcontroller device bringing Raspberry Pi quality, cost, and easy of use to the microcontroller space. The areas marked KEEPOUT in pcb silkscreen should not have traces running through them to avoid shorts on a soldered in module!
